// Logisim project 3-User-Buzzer-System.circ as structural Verilog: 1 circuit, main circuit main
module main (
);

  wire Buzzer1_out, Buzzer2_out, Buzzer3_out, FF2_p10, FF2_p11, NOT_LOCK_p1, NOT_LOCK_p2, NOT_LOCK_p3,
       NOT_LOCK_p4, Reset_out, SET1_p2, SET1_p4, SET1_p8, SET2_p11;

  Button Buzzer1 (.out(Buzzer1_out));
  Button Buzzer2 (.out(Buzzer2_out));
  Button Buzzer3 (.out(Buzzer3_out));
  Button Reset (.out(Reset_out));
  // AND_Gate SET1: pin names not known; wires that end beside it: Buzzer1_out, SET1_p2, Buzzer2_out, SET1_p4, 1'b1, Reset_out, 1'b1, SET1_p8
  // AND_Gate SET2: pin names not known; wires that end beside it: SET1_p2, Buzzer2_out, SET1_p2, Buzzer3_out, SET1_p8, SET1_p4, Reset_out, 1'b1, Reset_out, 1'b1, SET2_p11
  // AND_Gate SET3: pin names not known; wires that end beside it: 1'b1, SET1_p2, Buzzer3_out, SET1_p2, SET2_p11, SET1_p8, Reset_out, Reset_out
  // D_Flip_Flop FF1: pin names not known; wires that end beside it: Buzzer1_out, SET1_p2, Buzzer2_out, 1'b1, SET1_p4, Reset_out, 1'b1, SET1_p8, Reset_out
  // D_Flip_Flop FF2: pin names not known; wires that end beside it: Buzzer2_out, SET1_p2, Buzzer3_out, 1'b1, SET1_p8, Reset_out, 1'b1, SET2_p11, Reset_out, FF2_p10, FF2_p11
  // D_Flip_Flop FF3: pin names not known; wires that end beside it: Buzzer3_out, SET1_p2, 1'b1, SET2_p11, Reset_out
  // NOT_Gate NOT_LOCK: pin names not known; wires that end beside it: NOT_LOCK_p1, NOT_LOCK_p2, NOT_LOCK_p3, NOT_LOCK_p4, NOT_LOCK_p4, SET1_p2
  or LOCK (NOT_LOCK_p2, FF2_p10, FF2_p11);
  LED #(.oncolor("#00ff00")) Winner1 (.in(NOT_LOCK_p1));
  LED #(.oncolor("#00ff00")) Winner2 (.in(NOT_LOCK_p2));
  LED #(.oncolor("#00ff00")) Winner3 (.in(NOT_LOCK_p3));
  // Counter #(.width(8)) Count1: pin names not known; wires that end beside it: SET1_p4, SET1_p8
  // Counter #(.width(8)) Count2: pin names not known; wires that end beside it: SET1_p8, SET2_p11
  // Counter #(.width(8)) Count3: pin names not known; wires that end beside it: SET2_p11
endmodule
