// Logisim project project1.circ as structural Verilog: 1 circuit, main circuit main
module main (
);

  wire and_1_out, and_2_out, and_3_out, Buzzer1_out, Buzzer2_out, Buzzer3_out, CounterReset_out, FF1_q,
       FF1_qn, FF2_q, FF2_qn, FF3_q, FF3_qn, not_1_out, or_1_out, Reset_out;
  wire [3:0] Counter1_q, counter_1_q, counter_2_q;

  Button Buzzer1 (.out(Buzzer1_out));
  Button Buzzer2 (.out(Buzzer2_out));
  Button Buzzer3 (.out(Buzzer3_out));
  Button Reset (.out(Reset_out));
  and and_1 (and_1_out, Buzzer1_out, not_1_out);
  and and_2 (and_2_out, Buzzer2_out, not_1_out);
  and and_3 (and_3_out, Buzzer3_out, not_1_out);
  D_Flip_Flop FF1 (.D(1'b1), .clk(and_1_out), .Q(FF1_q), .Qn(FF1_qn), .reset(Reset_out));  // open: preset
  LED #(.active("false")) Winner1 (.in(FF1_qn));
  D_Flip_Flop FF2 (.D(1'b1), .clk(and_2_out), .Q(FF2_q), .Qn(FF2_qn), .reset(Reset_out));  // open: preset
  LED #(.active("false")) Winner2 (.in(FF2_qn));
  D_Flip_Flop FF3 (.D(1'b1), .clk(and_3_out), .Q(FF3_q), .Qn(FF3_qn), .reset(Reset_out));  // open: preset
  LED #(.active("false")) Winner3 (.in(FF3_qn));
  or or_1 (or_1_out, FF1_q, FF2_q, FF3_q);
  not not_1 (not_1_out, or_1_out);
  Button CounterReset (.out(CounterReset_out));
  Counter #(.max('hf), .width(4)) Counter1 (
    .clr(CounterReset_out), .clk(and_1_out), .Q(Counter1_q));  // open: load, up, count, D, carry
  Counter #(.max('hf), .width(4)) counter_1 (
    .clr(CounterReset_out), .clk(and_2_out), .Q(counter_1_q));  // open: load, up, count, D, carry
  Counter #(.max('hf), .width(4)) counter_2 (
    .clr(CounterReset_out), .clk(and_3_out), .Q(counter_2_q));  // open: load, up, count, D, carry
  Hex_Digit_Display W1 (.value(Counter1_q));  // open: dp
  Hex_Digit_Display hex_digit_display_1 (.value(counter_1_q));  // open: dp
  Hex_Digit_Display hex_digit_display_2 (.value(counter_2_q));  // open: dp
endmodule
